# Fritzing sketch TrafficLight-SevenSegment (saved by Fritzing 0.9.3b)
circuit board: 8.39237cm x 9.18888cm
breadboards: 1

parts:
  LED2 = LED - 5mm [color="Yellow (585nm)" package="5 mm [THT]"]
  DI1 = 7 Segment Display
  LED1 = LED - 5mm [color="Red (633nm)" package="5 mm [THT]"]
  LED3 = LED - 5mm [color="Green (555nm)" package="5 mm [THT]"]
  R1 = Resistor [tolerance=±5% resistance=220 package=THT]
  Rsa = Resistor [tolerance=±5% resistance=220 package=THT]
  Rsb = Resistor [tolerance=±5% resistance=220 package=THT]
  Rsc = Resistor [tolerance=±5% resistance=220 package=THT]
  Rsd = Resistor [tolerance=±5% resistance=220 package=THT]
  Rse = Resistor [tolerance=±5% resistance=220 package=THT]
  Rsf = Resistor [tolerance=±5% resistance=220 package=THT]
  Rsg = Resistor [tolerance=±5% resistance=220 package=THT]
  Part1 = Arduino Uno (Rev3)

nets:
  N1: LED2.cathode, LED1.cathode, LED3.cathode, R1.Pin_1
  N2: LED2.anode, Part1.D11_PWM/MOSI
  N3: DI1.Segment_E, Rse.Pin_1
  N4: DI1.Segment_D, Rsd.Pin_1
  N5: DI1.common_anode, Part1.3V3
  N6: DI1.Segment_C, Rsc.Pin_0
  N7: DI1.Segment_B, Rsb.Pin_0
  N8: DI1.Segment_A, Rsa.Pin_0
  N9: DI1.Segment_F, Rsf.Pin_1
  N10: DI1.Segment_G, Rsg.Pin_1
  N11: LED1.anode, Part1.D10_PWM/SS
  N12: LED3.anode, Part1.D12/MISO
  N13: R1.Pin_0, Part1.GND
  N14: Rsa.Pin_1, Part1.D2
  N15: Rsb.Pin_1, Part1.D3_PWM
  N16: Rsc.Pin_1, Part1.D4
  N17: Rsd.Pin_0, Part1.D5_PWM
  N18: Rse.Pin_0, Part1.D6_PWM
  N19: Rsf.Pin_0, Part1.D7
  N20: Rsg.Pin_0, Part1.D8
